// Logisim project Bird.circ as structural Verilog: 15 circuits, main circuit main
module main (
  output [15:0] R0,
  output [15:0] R1,
  output [15:0] R2,
  output [15:0] R3,
  output [15:0] R4,
  output [15:0] R5,
  output [15:0] R6,
  output [15:0] R7
);

  wire AluZF, clk, DATAMUX, IRLD, MEMLD, MUX, not_1_out, PCINC, PCLD, PCMUX, REGLD, SP_minus_minus,
       SP_plus_plus, ZF, ZFLD;
  wire [1:0] ARMUX;
  wire [2:0] Dst;
  wire [5:0] AluCode;
  wire [5:3] IR;
  wire [11:0] adder_1_out, AddrOut, multiplexer_2_out, PcOut, Src2_12;
  wire [15:0] AluResult, bit_extender_1_out, DataOut, MemOut, multiplexer_4_out, Result;
  wire [15:12] Src2_16;

  Clock clock_1 (.out(clk));
  Multiplexer #(.select(2), .width(12), .enable("false")) multiplexer_1 (
    .in0(PcOut), .in1(Src2_12), .in2(R7[11:0]), .out(AddrOut), .sel(ARMUX));  // open: in3
  PC pc_1 (.Din(multiplexer_2_out), .PCINC(PCINC), .PCLD(PCLD), .Dout(PcOut));
  Multiplexer #(.width(12), .enable("false")) multiplexer_2 (
    .in0(adder_1_out), .in1({AluCode, IR, Dst}), .out(multiplexer_2_out), .sel(PCMUX));
  Adder #(.width(12)) adder_1 (.a(PcOut), .b({AluCode, IR, Dst}), .out(adder_1_out));  // open: cin, cout
  Multiplexer #(.width(16), .enable("false")) multiplexer_3 (.in0(AluResult), .in1(MemOut), .out(Result), .sel(MUX));
  RegBank regbank_1 (
    .Din(Result), .REGSEL(Dst), .REGLD(REGLD), .SP_minus_minus(SP_minus_minus), .SP_plus_plus(SP_plus_plus),
    .R0(R0), .R1(R1), .R2(R2), .R3(R3), .R4(R4), .R5(R5), .R6(R6), .R7(R7));
  _1_bit_Reg u_1_bit_reg_1 (.Din(AluZF), .LD(ZFLD), .Dout(ZF));
  CU cu_1 (
    .Opcode(MemOut[15:12]), .ZF(ZF), .DATAMUX(DATAMUX), .PCMUX(PCMUX), .SP_plus_plus(SP_plus_plus),
    .SP_minus_minus(SP_minus_minus), .IRLD(IRLD), .MUX(MUX), .REGLD(REGLD), .PCINC(PCINC), .PCLD(PCLD),
    .ZFLD(ZFLD), .MEMLD(MEMLD), .ARMUX(ARMUX));
  not not_1 (not_1_out, MEMLD);
  Multiplexer #(.select(3), .width(16), .enable("false")) multiplexer_4 (
    .in0(R0), .in1(R1), .in2(R2), .in3(R3), .in4(R4), .in5(R5), .in6(R6), .in7(R7), .out(multiplexer_4_out),
    .sel(AluCode[2:0]));
  RAM #(.addrWidth(12), .dataWidth(16), .bus("separate")) ram_1 (
    .addr(AddrOut), .din(DataOut), .data(MemOut), .str(MEMLD), .clk(clk), .ld(not_1_out));  // open: sel, clr
  Multiplexer #(.select(3), .width(16), .enable("false")) multiplexer_5 (
    .in0(R0), .in1(R1), .in2(R2), .in3(R3), .in4(R4), .in5(R5), .in6(R6), .in7(R7), .out({Src2_16, Src2_12}),
    .sel(IR));
  ALU alu_1 (.A(multiplexer_4_out), .B({Src2_16, Src2_12}), .AluOp(AluCode), .AluResult(AluResult), .ZF(AluZF));
  IR ir_1 (.Din(MemOut[11:0]), .LD(IRLD), .Dout({AluCode, IR, Dst}));
  Multiplexer #(.width(16), .enable("false")) multiplexer_6 (
    .in0({Src2_16, Src2_12}), .in1(bit_extender_1_out), .out(DataOut), .sel(DATAMUX));
  assign bit_extender_1_out = {{4{1'b0}}, PcOut};  // Bit_Extender bit_extender_1

  // Other names for the same wires on the sheet: IR (some bits) = {AluCode, Dst}; Src1[2:0] = AluCode[2:0];
  //   Src2[2:0] = IR; Opcode[3:0] = MemOut[15:12]; Reg0[15:0] = R0; Reg1[15:0] = R1; Reg2[15:0] = R2; Reg3[15:0] = R3;
  //   Reg4[15:0] = R4; Reg5[15:0] = R5; Reg6[15:0] = R6; R7_12[11:0] = R7[11:0]; R7_16[15:0] = R7; Reg7[15:0] = R7;
  //   Src2_16[11:0] = Src2_12

  // Notes on the sheet:
  //   Memory
endmodule

module _1_bit_Reg (
  input  Din,
  input  LD,
  output Dout
);

  wire and_1_out, and_2_out, Clk_out;

  Clock Clk (.out(Clk_out));
  and and_1 (and_1_out, Din, LD);
  and and_2 (and_2_out, ~Din, LD);  // AND_Gate
  S_R_Flip_Flop s_r_ff_1 (.S(and_1_out), .clk(Clk_out), .R(and_2_out), .Q(Dout));  // open: Qn, preset, reset, en
endmodule

module _2_bits_Reg (
  input  [1:0] Din,
  input  LD,
  output [1:0] Dout
);

  _1_bit_Reg u_1_bit_reg_1 (.Din(Din[0]), .LD(LD), .Dout(Dout[0]));
  _1_bit_Reg u_1_bit_reg_2 (.Din(Din[1]), .LD(LD), .Dout(Dout[1]));
endmodule

module _4_bits_Reg (
  input  [3:0] Din,
  input  LD,
  output [3:0] Dout
);

  _2_bits_Reg u_2_bits_reg_1 (.Din(Din[1:0]), .LD(LD), .Dout(Dout[1:0]));
  _2_bits_Reg u_2_bits_reg_2 (.Din(Din[3:2]), .LD(LD), .Dout(Dout[3:2]));
endmodule

module _8_bits_Reg (
  input  [7:0] Din,
  input  LD,
  output [7:0] Dout
);

  _4_bits_Reg u_4_bits_reg_1 (.Din(Din[3:0]), .LD(LD), .Dout(Dout[3:0]));
  _4_bits_Reg u_4_bits_reg_2 (.Din(Din[7:4]), .LD(LD), .Dout(Dout[7:4]));
endmodule

module _10_bits_Reg (
  input  [9:0] Din,
  input  LD,
  output [9:0] Dout
);

  _8_bits_Reg u_8_bits_reg_1 (.Din(Din[7:0]), .LD(LD), .Dout(Dout[7:0]));
  _2_bits_Reg u_2_bits_reg_1 (.Din(Din[9:8]), .LD(LD), .Dout(Dout[9:8]));
endmodule

module _12_bits_Reg (
  input  [11:0] Din,
  input  LD,
  output [11:0] Dout
);

  _8_bits_Reg u_8_bits_reg_1 (.Din(Din[7:0]), .LD(LD), .Dout(Dout[7:0]));
  _4_bits_Reg u_4_bits_reg_1 (.Din(Din[11:8]), .LD(LD), .Dout(Dout[11:8]));
endmodule

module _16_bits_Reg (
  input  [15:0] Din,
  input  LD,
  output [15:0] Dout
);

  _8_bits_Reg u_8_bits_reg_1 (.Din(Din[7:0]), .LD(LD), .Dout(Dout[7:0]));
  _8_bits_Reg u_8_bits_reg_2 (.Din(Din[15:8]), .LD(LD), .Dout(Dout[15:8]));
endmodule

module Reg6 (
  input  [15:0] Din,
  input  INC,
  input  LD,
  output [15:0] Dout
);

  wire or_1_out;
  wire [15:0] adder_1_out, multiplexer_1_out;

  Multiplexer #(.width(16), .enable("false")) multiplexer_1 (
    .in0(Din), .in1(adder_1_out), .out(multiplexer_1_out), .sel(INC));
  or or_1 (or_1_out, INC, LD);
  _16_bits_Reg u_16_bits_reg_1 (.Din(multiplexer_1_out), .LD(or_1_out), .Dout(Dout));
  Adder #(.width(16)) adder_1 (.a(16'h1), .b(Dout), .out(adder_1_out));  // open: cin, cout
endmodule

module Reg7 (
  input  [15:0] Din,
  input  DEC,
  input  INC,
  input  LD,
  output [15:0] Dout
);

  wire or_1_out;
  wire [15:0] adder_1_out, multiplexer_1_out, subtractor_1_out;

  Multiplexer #(.select(2), .width(16), .enable("false")) multiplexer_1 (
    .in0(Din), .in1(adder_1_out), .in2(subtractor_1_out), .out(multiplexer_1_out), .sel({DEC, INC}));  // open: in3
  or or_1 (or_1_out, DEC, INC, LD);
  Subtractor #(.width(16)) subtractor_1 (.a(Dout), .b(16'h1), .out(subtractor_1_out));  // open: bin, bout
  Adder #(.width(16)) adder_1 (.a(16'h1), .b(Dout), .out(adder_1_out));  // open: cin, cout
  _16_bits_Reg u_16_bits_reg_1 (.Din(multiplexer_1_out), .LD(or_1_out), .Dout(Dout));
endmodule

module RegBank (
  input  [15:0] Din,
  input  [2:0] REGSEL,
  input  REGLD,
  input  SP_minus_minus,
  input  SP_plus_plus,
  output [15:0] R0,
  output [15:0] R1,
  output [15:0] R2,
  output [15:0] R3,
  output [15:0] R4,
  output [15:0] R5,
  output [15:0] R6,
  output [15:0] R7
);

  wire and_1_out, and_2_out, and_3_out, and_4_out, and_5_out, and_6_out, and_7_out, and_8_out,
       decoder_1_out0, decoder_1_out1, decoder_1_out2, decoder_1_out3, decoder_1_out4, decoder_1_out5,
       decoder_1_out6, decoder_1_out7;

  Decoder #(.select(3), .enable("false")) decoder_1 (
    .out0(decoder_1_out0), .out1(decoder_1_out1), .out2(decoder_1_out2), .out3(decoder_1_out3),
    .out4(decoder_1_out4), .out5(decoder_1_out5), .out6(decoder_1_out6), .out7(decoder_1_out7), .sel(REGSEL));
  and and_1 (and_1_out, decoder_1_out0, REGLD);
  and and_2 (and_2_out, decoder_1_out1, REGLD);
  and and_3 (and_3_out, decoder_1_out2, REGLD);
  and and_4 (and_4_out, decoder_1_out3, REGLD);
  and and_5 (and_5_out, decoder_1_out4, REGLD);
  and and_6 (and_6_out, decoder_1_out5, REGLD);
  and and_7 (and_7_out, decoder_1_out6, REGLD);
  and and_8 (and_8_out, decoder_1_out7, REGLD);
  _16_bits_Reg u_16_bits_reg_1 (.Din(Din), .LD(and_1_out), .Dout(R0));
  _16_bits_Reg u_16_bits_reg_2 (.Din(Din), .LD(and_2_out), .Dout(R1));
  _16_bits_Reg u_16_bits_reg_3 (.Din(Din), .LD(and_3_out), .Dout(R2));
  _16_bits_Reg u_16_bits_reg_4 (.Din(Din), .LD(and_4_out), .Dout(R3));
  _16_bits_Reg u_16_bits_reg_5 (.Din(Din), .LD(and_5_out), .Dout(R4));
  _16_bits_Reg u_16_bits_reg_6 (.Din(Din), .LD(and_6_out), .Dout(R5));
  _16_bits_Reg u_16_bits_reg_7 (.Din(Din), .LD(and_7_out), .Dout(R6));
  Reg7 reg7_1 (.Din(Din), .DEC(SP_minus_minus), .INC(SP_plus_plus), .LD(and_8_out), .Dout(R7));
endmodule

module ALU (
  input  [15:0] A,
  input  [15:0] B,
  input  [5:0] AluOp,
  output [15:0] AluResult,
  output ZF
);

  wire [15:0] adder_1_out, adder_2_out, and_1_out, multiplexer_1_out, not_1_out, or_1_out, subtractor_1_out,
       subtractor_2_out, xor_1_out;

  Adder #(.width(16)) adder_1 (.a(A), .b(B), .out(adder_1_out));  // open: cin, cout
  Subtractor #(.width(16)) subtractor_1 (.a(A), .b(B), .out(subtractor_1_out));  // open: bin, bout
  assign and_1_out = A & B;  // AND_Gate and_1, 16 bits wide
  assign or_1_out = A | B;  // OR_Gate or_1, 16 bits wide
  assign xor_1_out = A ^ B;  // XOR_Gate xor_1, 16 bits wide
  assign not_1_out = ~B;  // NOT_Gate not_1, 16 bits wide
  Adder #(.width(16)) adder_2 (.a(B), .b(16'h1), .out(adder_2_out));  // open: cin, cout
  Subtractor #(.width(16)) subtractor_2 (.a(B), .b(16'h1), .out(subtractor_2_out));  // open: bin, bout
  Multiplexer #(.select(3), .width(16), .enable("false")) multiplexer_1 (
    .in0(not_1_out), .in1(B), .in2(adder_2_out), .in3(subtractor_2_out), .out(multiplexer_1_out),
    .sel({1'b0, AluOp[1:0]}));  // open: in4, in5, in6, in7
  Multiplexer #(.select(3), .width(16), .enable("false")) multiplexer_2 (
    .in0(adder_1_out), .in1(subtractor_1_out), .in2(and_1_out), .in3(or_1_out), .in4(xor_1_out),
    .in7(multiplexer_1_out), .out(AluResult), .sel(AluOp[5:3]));  // open: in5, in6
  nor nor_1 (ZF, AluResult[0], AluResult[1], AluResult[2], AluResult[3], AluResult[4], AluResult[5], AluResult[6], AluResult[7], AluResult[9], AluResult[10], AluResult[11], AluResult[12], AluResult[13], AluResult[14], AluResult[15], AluResult[8]);

  // Notes on the sheet:
  //   Adder
  //   Substractor
  //   Bitwise AND
  //   Bitwise OR
  //   Bitwise XOR
  //   Bitwise NOT
  //   Move
  //   Increment
  //   Decrement
endmodule

module PC (
  input  [11:0] Din,
  input  PCINC,
  input  PCLD,
  output [11:0] Dout
);

  wire or_1_out;
  wire [11:0] adder_1_out, multiplexer_1_out;

  Adder #(.width(12)) adder_1 (.a(Dout), .b(12'h1), .out(adder_1_out));  // open: cin, cout
  Multiplexer #(.width(12), .enable("false")) multiplexer_1 (
    .in0(Din), .in1(adder_1_out), .out(multiplexer_1_out), .sel(PCINC));
  or or_1 (or_1_out, PCINC, PCLD);
  _12_bits_Reg u_12_bits_reg_1 (.Din(multiplexer_1_out), .LD(or_1_out), .Dout(Dout));
endmodule

module IR (
  input  [11:0] Din,
  input  LD,
  output [11:0] Dout
);

  _8_bits_Reg u_8_bits_reg_1 (.Din(Din[7:0]), .LD(LD), .Dout(Dout[7:0]));
  _4_bits_Reg u_4_bits_reg_1 (.Din(Din[11:8]), .LD(LD), .Dout(Dout[11:8]));
endmodule

module CU (
  input  [3:0] Opcode,
  input  ZF,
  output IRLD,
  output MEMLD,
  output MUX,
  output ZFLD,
  output REGLD,
  output [1:0] ARMUX,
  output PCINC,
  output PCLD,
  output SP_minus_minus,
  output SP_plus_plus,
  output PCMUX,
  output DATAMUX
);

  wire [1:1] and_1_out;
  wire [3:0] multiplexer_1_out, multiplexer_2_out, n4_bits_reg_1_dout;
  wire [17:0] Dout;

  and and_1 (and_1_out[1], ~Opcode[0], ~Opcode[1], Opcode[2], ~Opcode[3]);  // AND_Gate
  Multiplexer #(.width(4), .enable("false")) multiplexer_1 (
    .in0(Dout[3:0]), .in1(multiplexer_2_out), .out(multiplexer_1_out), .sel(Dout[17]));
  Multiplexer #(.select(2), .width(4), .enable("false")) multiplexer_2 (
    .in0(Opcode), .in1(Opcode), .in2(4'b0000), .in3(4'b0101), .out(multiplexer_2_out),
    .sel({and_1_out[1], ZF}));
  _4_bits_Reg u_4_bits_reg_1 (.Din(multiplexer_1_out), .LD(1'b1), .Dout(n4_bits_reg_1_dout));
  ROM #(.addrWidth(4), .dataWidth(18)) rom_1 (
    .addr(n4_bits_reg_1_dout),
    .data({Dout[17], DATAMUX, PCMUX, SP_plus_plus, SP_minus_minus, PCLD, PCINC, ARMUX, REGLD, ZFLD, MUX, MEMLD, IRLD, Dout[3:0]}));  // open: sel

  // Other names for the same wires on the sheet: Next[3:0] = Dout[3:0];
  //   Dout[16:4] = {DATAMUX, PCMUX, SP_plus_plus, SP_minus_minus, PCLD, PCINC, ARMUX, REGLD, ZFLD, MUX, MEMLD, IRLD};
  //   FETCH = Dout[17]

  // Notes on the sheet:
  //   contents of rom_1 (hex, n*v repeats v):
  //   20810 940 340 220 0 1000 0 180 2420 400c 13420 400d 540 9400
endmodule
