// Logisim project Frog.circ as structural Verilog: 15 circuits, main circuit main
module main (
  output [15:0] out_1,
  output [15:0] out_2,
  output [15:0] out_3
);

  wire control_unit_1_irld, control_unit_1_mux, control_unit_1_pcinc, control_unit_1_regld;
  wire [2:0] ir_1_dout, ir_1_dout_3;
  wire [5:0] ir_1_dout_2;
  wire [9:0] n10bit_pc_1_dout;
  wire [15:0] alu_1_dout, multiplexer_1_out, multiplexer_2_out, multiplexer_3_out,
       n8_16bit_register_bank_1_r3, n8_16bit_register_bank_1_r4, n8_16bit_register_bank_1_r5,
       n8_16bit_register_bank_1_r6, n8_16bit_register_bank_1_r7, rom_1_data;

  _10bit_PC u_10bit_pc_1 (.PCINC(control_unit_1_pcinc), .Dout(n10bit_pc_1_dout));  // open: Din
  _8_16bit_Register_Bank u_8_16bit_register_bank_1 (
    .Din(multiplexer_2_out), .REGSEL(ir_1_dout), .REGLD(control_unit_1_regld), .R0(out_1), .R1(out_2),
    .R2(out_3), .R3(n8_16bit_register_bank_1_r3), .R4(n8_16bit_register_bank_1_r4),
    .R5(n8_16bit_register_bank_1_r5), .R6(n8_16bit_register_bank_1_r6), .R7(n8_16bit_register_bank_1_r7));  // open: INC6, DEC7, INC7
  ROM #(.addrWidth(10), .dataWidth(16)) rom_1 (.addr(n10bit_pc_1_dout), .data(rom_1_data), .sel(1'b1));
  Multiplexer #(.select(3), .width(16), .enable("false")) multiplexer_1 (
    .in0(out_1), .in1(out_2), .in2(out_3), .in3(n8_16bit_register_bank_1_r3),
    .in4(n8_16bit_register_bank_1_r4), .in5(n8_16bit_register_bank_1_r5), .in6(n8_16bit_register_bank_1_r6),
    .in7(n8_16bit_register_bank_1_r7), .out(multiplexer_1_out), .sel(ir_1_dout_3));
  Multiplexer #(.width(16), .enable("false")) multiplexer_2 (
    .in0(alu_1_dout), .in1(rom_1_data), .out(multiplexer_2_out), .sel(control_unit_1_mux));
  Multiplexer #(.select(3), .width(16), .enable("false")) multiplexer_3 (
    .in0(out_1), .in1(out_2), .in2(out_3), .in3(n8_16bit_register_bank_1_r3),
    .in4(n8_16bit_register_bank_1_r4), .in5(n8_16bit_register_bank_1_r5), .in6(n8_16bit_register_bank_1_r6),
    .in7(n8_16bit_register_bank_1_r7), .out(multiplexer_3_out), .sel(ir_1_dout_2[5:3]));
  ALU alu_1 (
    .Din1(multiplexer_1_out), .Din2(multiplexer_3_out), .Dout(alu_1_dout), .ALUop(ir_1_dout_2));  // open: ZF__zero_flag
  Control_Unit control_unit_1 (
    .Din(rom_1_data[15:12]), .PCINC(control_unit_1_pcinc), .REGLD(control_unit_1_regld),
    .MUX(control_unit_1_mux), .IRLD(control_unit_1_irld));
  IR ir_1 (
    .Din(rom_1_data[11:0]), .LD(control_unit_1_irld),
    .Dout({ir_1_dout_2[2:0], ir_1_dout_3, ir_1_dout_2[5:3], ir_1_dout}));

  // Notes on the sheet:
  //   Data Memory
  //   contents of rom_1 (hex, n*v repeats v):
  //   2000 3 2001 2 2002 5 1008 1210 1e10 1e00
endmodule

module _1bit_SR_Reg (
  input  Din,
  input  LD,
  output Dout
);

  wire and_1_out, and_2_out, Clk_out;

  Clock Clk (.out(Clk_out));
  and and_1 (and_1_out, Din, LD);
  and and_2 (and_2_out, ~Din, LD);  // AND_Gate
  S_R_Flip_Flop s_r_ff_1 (.S(and_1_out), .clk(Clk_out), .R(and_2_out), .Q(Dout));  // open: Qn, preset, reset, en
endmodule

module _4bit_SR_Reg (
  input  [3:0] Din,
  input  LD,
  output [3:0] Dout
);

  _1bit_SR_Reg u_1bit_sr_reg_1 (.Din(Din[0]), .LD(LD), .Dout(Dout[0]));
  _1bit_SR_Reg u_1bit_sr_reg_2 (.Din(Din[1]), .LD(LD), .Dout(Dout[1]));
  _1bit_SR_Reg u_1bit_sr_reg_3 (.Din(Din[2]), .LD(LD), .Dout(Dout[2]));
  _1bit_SR_Reg u_1bit_sr_reg_4 (.Din(Din[3]), .LD(LD), .Dout(Dout[3]));
endmodule

module _8bit_SR_Reg (
  input  [7:0] Din,
  input  LD,
  output [7:0] Dout
);

  _4bit_SR_Reg u_4bit_sr_reg_1 (.Din(Din[3:0]), .LD(LD), .Dout(Dout[3:0]));
  _4bit_SR_Reg u_4bit_sr_reg_2 (.Din(Din[7:4]), .LD(LD), .Dout(Dout[7:4]));
endmodule

module _16bit_SR_Reg (
  input  [15:0] Din,
  input  LD,
  output [15:0] Dout
);

  _8bit_SR_Reg u_8bit_sr_reg_1 (.Din(Din[7:0]), .LD(LD), .Dout(Dout[7:0]));
  _8bit_SR_Reg u_8bit_sr_reg_2 (.Din(Din[15:8]), .LD(LD), .Dout(Dout[15:8]));
endmodule

module _8_16bit_Register_Bank (
  input  [15:0] Din,
  input  [2:0] REGSEL,
  input  REGLD,
  input  INC6,
  input  DEC7,
  input  INC7,
  output [15:0] R0,
  output [15:0] R1,
  output [15:0] R2,
  output [15:0] R3,
  output [15:0] R4,
  output [15:0] R5,
  output [15:0] R6,
  output [15:0] R7
);

  wire and_1_out, and_2_out, and_3_out, and_4_out, and_5_out, and_6_out, and_7_out, and_8_out,
       decoder_1_out0, decoder_1_out1, decoder_1_out2, decoder_1_out3, decoder_1_out4, decoder_1_out5,
       decoder_1_out6, decoder_1_out7;

  Decoder #(.select(3), .enable("false")) decoder_1 (
    .out0(decoder_1_out0), .out1(decoder_1_out1), .out2(decoder_1_out2), .out3(decoder_1_out3),
    .out4(decoder_1_out4), .out5(decoder_1_out5), .out6(decoder_1_out6), .out7(decoder_1_out7), .sel(REGSEL));
  and and_1 (and_1_out, decoder_1_out0, REGLD);
  and and_2 (and_2_out, decoder_1_out1, REGLD);
  and and_3 (and_3_out, decoder_1_out2, REGLD);
  and and_4 (and_4_out, decoder_1_out3, REGLD);
  and and_5 (and_5_out, decoder_1_out4, REGLD);
  and and_6 (and_6_out, decoder_1_out5, REGLD);
  and and_7 (and_7_out, decoder_1_out6, REGLD);
  and and_8 (and_8_out, decoder_1_out7, REGLD);
  _16bit_SR_Reg u_16bit_sr_reg_1 (.Din(Din), .LD(and_1_out), .Dout(R0));
  _16bit_SR_Reg u_16bit_sr_reg_2 (.Din(Din), .LD(and_2_out), .Dout(R1));
  _16bit_SR_Reg u_16bit_sr_reg_3 (.Din(Din), .LD(and_3_out), .Dout(R2));
  _16bit_SR_Reg u_16bit_sr_reg_4 (.Din(Din), .LD(and_4_out), .Dout(R3));
  _16bit_SR_Reg u_16bit_sr_reg_5 (.Din(Din), .LD(and_5_out), .Dout(R4));
  _16bit_SR_Reg u_16bit_sr_reg_6 (.Din(Din), .LD(and_6_out), .Dout(R5));
  _16bit_reg_w_inc u_16bit_reg_w_inc_1 (.Din(Din), .INC(INC6), .LD(and_7_out), .Dout(R6));
  _16bit_reg_w_inc___dec u_16bit_reg_w_inc_dec_1 (.Din(Din), .DEC(DEC7), .INC(INC7), .LD(and_8_out), .Dout(R7));

  // Notes on the sheet:
  //   0
  //   1
  //   2
  //   3
  //   4
  //   5
endmodule

module _1bit_reg_w_inc (
  input  Din,
  input  INC,
  input  LD,
  output Dout
);

  wire adder_1_out, multiplexer_1_out, or_1_out;

  Multiplexer #(.enable("false")) multiplexer_1 (.in0(Din), .in1(adder_1_out), .out(multiplexer_1_out), .sel(INC));
  or or_1 (or_1_out, INC, LD);
  Adder #(.width(1)) adder_1 (.a(1'b1), .b(Dout), .out(adder_1_out));  // open: cin, cout
  _1bit_SR_Reg u_1bit_sr_reg_1 (.Din(multiplexer_1_out), .LD(or_1_out), .Dout(Dout));
endmodule

module _1bit_reg_w_inc___dec (
  input  Din,
  input  DEC,
  input  INC,
  input  LD,
  output Dout
);

  wire adder_1_out, multiplexer_1_out, or_1_out, subtractor_1_out;

  Multiplexer #(.select(2), .enable("false")) multiplexer_1 (
    .in0(Din), .in1(adder_1_out), .in2(subtractor_1_out), .in3(1'b0), .out(multiplexer_1_out),
    .sel({DEC, INC}));
  _1bit_SR_Reg u_1bit_sr_reg_1 (.Din(multiplexer_1_out), .LD(or_1_out), .Dout(Dout));
  or or_1 (or_1_out, DEC, INC, LD);
  Subtractor #(.width(1)) subtractor_1 (.a(1'b1), .b(Dout), .out(subtractor_1_out));  // open: bin, bout
  Adder #(.width(1)) adder_1 (.a(1'b1), .b(Dout), .out(adder_1_out));  // open: cin, cout
endmodule

module _16bit_reg_w_inc (
  input  [15:0] Din,
  input  INC,
  input  LD,
  output [15:0] Dout
);

  wire or_1_out;
  wire [15:0] adder_1_out, multiplexer_1_out;

  Multiplexer #(.width(16), .enable("false")) multiplexer_1 (
    .in0(Din), .in1(adder_1_out), .out(multiplexer_1_out), .sel(INC));
  or or_1 (or_1_out, INC, LD);
  _16bit_SR_Reg u_16bit_sr_reg_1 (.Din(multiplexer_1_out), .LD(or_1_out), .Dout(Dout));
  Adder #(.width(16)) adder_1 (.a(16'h1), .b(Dout), .out(adder_1_out));  // open: cin, cout
endmodule

module _16bit_reg_w_inc___dec (
  input  [15:0] Din,
  input  DEC,
  input  INC,
  input  LD,
  output [15:0] Dout
);

  wire or_1_out;
  wire [15:0] adder_1_out, multiplexer_1_out, subtractor_1_out;

  Multiplexer #(.select(2), .width(16), .enable("false")) multiplexer_1 (
    .in0(Din), .in1(adder_1_out), .in2(subtractor_1_out), .out(multiplexer_1_out), .sel({DEC, INC}));  // open: in3
  or or_1 (or_1_out, DEC, INC, LD);
  Subtractor #(.width(16)) subtractor_1 (.a(Dout), .b(16'h1), .out(subtractor_1_out));  // open: bin, bout
  Adder #(.width(16)) adder_1 (.a(16'h1), .b(Dout), .out(adder_1_out));  // open: cin, cout
  _16bit_SR_Reg u_16bit_sr_reg_1 (.Din(multiplexer_1_out), .LD(or_1_out), .Dout(Dout));
endmodule

module ALU (
  input  [15:0] Din1,
  input  [15:0] Din2,
  input  [5:0] ALUop,
  output ZF__zero_flag,
  output [15:0] Dout
);

  wire [15:0] adder_1_out, adder_2_out, and_1_out, multiplexer_1_out, not_1_out, or_1_out, subtractor_1_out,
       subtractor_2_out, xor_1_out;

  Adder #(.width(16)) adder_1 (.a(Din1), .b(Din2), .out(adder_1_out));  // open: cin, cout
  Subtractor #(.width(16)) subtractor_1 (.a(Din1), .b(Din2), .out(subtractor_1_out));  // open: bin, bout
  assign and_1_out = Din1 & Din2;  // AND_Gate and_1, 16 bits wide
  assign or_1_out = Din1 | Din2;  // OR_Gate or_1, 16 bits wide
  assign xor_1_out = Din1 ^ Din2;  // XOR_Gate xor_1, 16 bits wide
  assign not_1_out = ~Din1;  // NOT_Gate not_1, 16 bits wide
  Adder #(.width(16)) adder_2 (.a(Din1), .b(16'h1), .out(adder_2_out));  // open: cin, cout
  Subtractor #(.width(16)) subtractor_2 (.a(Din1), .b(16'h1), .out(subtractor_2_out));  // open: bin, bout
  Multiplexer #(.select(3), .width(16), .enable("false")) multiplexer_1 (
    .in0(not_1_out), .in1(Din1), .in2(adder_2_out), .in3(subtractor_2_out), .out(multiplexer_1_out),
    .sel(ALUop[5:3]));  // open: in4, in5, in6, in7
  Multiplexer #(.select(3), .width(16), .enable("false")) multiplexer_2 (
    .in0(adder_1_out), .in1(subtractor_1_out), .in2(and_1_out), .in3(or_1_out), .in4(xor_1_out),
    .in7(multiplexer_1_out), .out(Dout), .sel(ALUop[2:0]));  // open: in5, in6
  nor nor_1 (ZF__zero_flag, Dout[0], Dout[1], Dout[2], Dout[3], Dout[4], Dout[5], Dout[6], Dout[7], Dout[8], Dout[9], Dout[10], Dout[11], Dout[12], Dout[13], Dout[14], Dout[15]);
endmodule

module _10bit_PC (
  input  [9:0] Din,
  input  PCINC,
  output [9:0] Dout
);

  wire CLK_out;
  wire [9:0] adder_1_out, multiplexer_1_out;

  Adder #(.width(10)) adder_1 (.a(Dout), .b(10'h1), .out(adder_1_out));  // open: cin, cout
  Clock CLK (.out(CLK_out));
  Multiplexer #(.width(10), .enable("false")) multiplexer_1 (
    .in0(Din), .in1(adder_1_out), .out(multiplexer_1_out), .sel(PCINC));
  Register #(.width(10)) Register (.D(multiplexer_1_out), .Q(Dout), .clk(CLK_out));  // open: en, clr
endmodule

module Control_Unit (
  input  [3:0] Din,
  output PCINC,
  output REGLD,
  output MUX,
  output IRLD
);

  wire [1:0] multiplexer_1_out, n2bit_sr_register_1_dout;
  wire [4:4] rom_1_data;

  Multiplexer #(.width(2), .enable("false")) multiplexer_1 (
    .in0(2'b00), .in1(Din[1:0]), .out(multiplexer_1_out), .sel(rom_1_data[4]));
  _2bit_SR_Register u_2bit_sr_register_1 (.Din(multiplexer_1_out), .LD(1'b1), .Dout(n2bit_sr_register_1_dout));
  ROM #(.addrWidth(2), .dataWidth(5)) rom_1 (
    .addr(n2bit_sr_register_1_dout), .data({rom_1_data[4], IRLD, MUX, REGLD, PCINC}), .sel(1'b1));

  // Notes on the sheet:
  //   contents of rom_1 (hex, n*v repeats v):
  //   19 2 7
  //   FETCH
endmodule

module IR (
  input  [11:0] Din,
  input  LD,
  output [11:0] Dout
);

  _8bit_SR_Reg u_8bit_sr_reg_1 (.Din(Din[7:0]), .LD(LD), .Dout(Dout[7:0]));
  _4bit_SR_Reg u_4bit_sr_reg_1 (.Din(Din[11:8]), .LD(LD), .Dout(Dout[11:8]));
endmodule

module _2bit_SR_Register (
  input  [1:0] Din,
  input  LD,
  output [1:0] Dout
);

  _1bit_SR_Reg u_1bit_sr_reg_1 (.Din(Din[0]), .LD(LD), .Dout(Dout[0]));
  _1bit_SR_Reg u_1bit_sr_reg_2 (.Din(Din[1]), .LD(LD), .Dout(Dout[1]));
endmodule
