// Logisim project Mammal.circ as structural Verilog: 21 circuits, main circuit main
module main (
  input  [15:0] Switch_1__Pol,
  input  [15:0] Switch_2__Int,
  input  [15:0] Switch_3__Int
);

  wire and_1_out, and_2_out, and_3_out, and_4_out, and_5_out, button_1_out, button_2_out, button_3_out,
       clock_1_out, cpu_1_intack, cpu_1_memld, inputdeviceint_1_int, inputdeviceint_2_int, not_1_out,
       not_2_out, not_3_out, not_4_out, not_5_out, not_6_out, not_7_out, not_8_out, not_9_out, not_10_out,
       not_11_out, not_12_out, not_13_out, not_14_out, not_15_out, not_16_out, not_17_out, not_18_out,
       not_19_out, not_20_out, not_21_out, not_22_out, not_23_out, not_24_out, not_25_out, not_26_out,
       not_27_out, not_28_out, not_29_out, not_30_out, not_31_out, not_32_out, not_33_out, not_34_out,
       not_35_out, not_36_out, not_37_out, PIC_interrupt;
  wire [3:0] n16_bits_reg_1_dout_2, n16_bits_reg_1_dout_3;
  wire [7:0] n16_bits_reg_1_dout;
  wire [10:0] cpu_1_addrbus;
  wire [11:11] cpu_1_addrbus_2;
  wire [15:0] cpu_1_data_out, inputdeviceint_1_dataout, inputdeviceint_2_dataout, inputdevicepol_1_dataout,
       multiplexer_1_out, multiplexer_2_out, multiplexer_3_out, multiplexer_4_out, multiplexer_5_out,
       PIC_device_id, ram_1_data;

  CPU cpu_1 (
    .INT(PIC_interrupt), .INTACK(cpu_1_intack), .MEMLD(cpu_1_memld),
    .ADDRBUS({cpu_1_addrbus_2[11], cpu_1_addrbus}), .DATA_OUT(cpu_1_data_out), .DATA_IN(multiplexer_1_out));
  Multiplexer #(.width(16), .enable("false")) multiplexer_1 (
    .in0(multiplexer_2_out), .in1(PIC_device_id), .out(multiplexer_1_out), .sel(cpu_1_intack));
  Clock clock_1 (.out(clock_1_out));
  Multiplexer #(.width(16), .enable("false")) multiplexer_2 (
    .in0(multiplexer_3_out), .in1(ram_1_data), .out(multiplexer_2_out), .sel(not_1_out));
  and and_1 (and_1_out, cpu_1_memld, not_1_out);
  not not_1 (not_1_out, cpu_1_addrbus_2[11]);
  RAM #(.addrWidth(11), .dataWidth(16), .bus("separate")) ram_1 (
    .addr(cpu_1_addrbus), .din(cpu_1_data_out), .data(ram_1_data), .str(and_1_out), .clk(clock_1_out));  // open: sel, ld, clr
  Multiplexer #(.width(16), .enable("false")) multiplexer_3 (
    .in0(multiplexer_4_out), .in1(inputdevicepol_1_dataout), .out(multiplexer_3_out), .sel(and_2_out));
  not not_2 (not_2_out, cpu_1_addrbus[10]);
  not not_3 (not_3_out, cpu_1_addrbus[8]);
  not not_4 (not_4_out, cpu_1_addrbus[9]);
  Button button_1 (.out(button_1_out));
  and and_2 (and_2_out, cpu_1_addrbus_2[11], not_2_out, not_4_out, not_3_out, not_6_out, not_7_out, not_9_out, not_8_out, not_5_out, not_10_out, not_11_out);
  not not_5 (not_5_out, cpu_1_addrbus[3]);
  not not_6 (not_6_out, cpu_1_addrbus[7]);
  not not_7 (not_7_out, cpu_1_addrbus[6]);
  not not_8 (not_8_out, cpu_1_addrbus[4]);
  not not_9 (not_9_out, cpu_1_addrbus[5]);
  not not_10 (not_10_out, cpu_1_addrbus[2]);
  not not_11 (not_11_out, cpu_1_addrbus[1]);
  InputDevicePol inputdevicepol_1 (
    .Data(Switch_1__Pol), .Button(button_1_out), .Ready(and_2_out), .A0(cpu_1_addrbus[0]),
    .DataOut(inputdevicepol_1_dataout));
  PIC PIC (
    .DEVICE_2(inputdeviceint_1_int), .DEVICE_3(inputdeviceint_2_int), .DEVICE_ID(PIC_device_id),
    .INTERRUPT(PIC_interrupt));  // open: DEVICE_0, DEVICE_1, DEVICE_4, DEVICE_5, DEVICE_6, DEVICE_7
  Multiplexer #(.width(16), .enable("false")) multiplexer_4 (
    .in0(multiplexer_5_out), .in1(inputdeviceint_1_dataout), .out(multiplexer_4_out), .sel(and_3_out));
  not not_12 (not_12_out, cpu_1_addrbus[9]);
  not not_13 (not_13_out, cpu_1_addrbus[10]);
  Button button_2 (.out(button_2_out));
  and and_3 (and_3_out, cpu_1_addrbus_2[11], not_13_out, not_12_out, cpu_1_addrbus[8], not_15_out, not_14_out, not_18_out, not_17_out, not_19_out, not_16_out, not_20_out);
  not not_14 (not_14_out, cpu_1_addrbus[6]);
  not not_15 (not_15_out, cpu_1_addrbus[7]);
  not not_16 (not_16_out, cpu_1_addrbus[2]);
  not not_17 (not_17_out, cpu_1_addrbus[4]);
  not not_18 (not_18_out, cpu_1_addrbus[5]);
  not not_19 (not_19_out, cpu_1_addrbus[3]);
  not not_20 (not_20_out, cpu_1_addrbus[1]);
  InputDeviceInt inputdeviceint_1 (
    .Data(Switch_2__Int), .Button(button_2_out), .Select(and_3_out), .DataOut(inputdeviceint_1_dataout),
    .INT(inputdeviceint_1_int));
  Multiplexer #(.width(16), .enable("false")) multiplexer_5 (
    .in0(16'habcd), .in1(inputdeviceint_2_dataout), .out(multiplexer_5_out), .sel(and_4_out));
  and and_4 (and_4_out, cpu_1_addrbus_2[11], not_22_out, cpu_1_addrbus[9], not_23_out, not_24_out, not_21_out, not_29_out, not_28_out, not_25_out, not_27_out, not_26_out);
  not not_21 (not_21_out, cpu_1_addrbus[6]);
  not not_22 (not_22_out, cpu_1_addrbus[10]);
  not not_23 (not_23_out, cpu_1_addrbus[8]);
  not not_24 (not_24_out, cpu_1_addrbus[7]);
  InputDeviceInt inputdeviceint_2 (
    .Data(Switch_3__Int), .Button(button_3_out), .Select(and_4_out), .DataOut(inputdeviceint_2_dataout),
    .INT(inputdeviceint_2_int));
  Button button_3 (.out(button_3_out));
  not not_25 (not_25_out, cpu_1_addrbus[3]);
  not not_26 (not_26_out, cpu_1_addrbus[1]);
  not not_27 (not_27_out, cpu_1_addrbus[2]);
  not not_28 (not_28_out, cpu_1_addrbus[4]);
  not not_29 (not_29_out, cpu_1_addrbus[5]);
  and and_5 (and_5_out, cpu_1_addrbus_2[11], not_34_out, cpu_1_addrbus[9], cpu_1_addrbus[8], not_31_out, not_33_out, not_35_out, not_32_out, not_30_out, not_36_out, not_37_out);
  not not_30 (not_30_out, cpu_1_addrbus[3]);
  not not_31 (not_31_out, cpu_1_addrbus[7]);
  not not_32 (not_32_out, cpu_1_addrbus[4]);
  not not_33 (not_33_out, cpu_1_addrbus[6]);
  not not_34 (not_34_out, cpu_1_addrbus[10]);
  not not_35 (not_35_out, cpu_1_addrbus[5]);
  Hex_Digit_Display hex_digit_display_1 (.value(n16_bits_reg_1_dout_2));  // open: dp
  Hex_Digit_Display hex_digit_display_2 (.value(n16_bits_reg_1_dout_3));  // open: dp
  _16_bits_Reg u_16_bits_reg_1 (
    .Din(cpu_1_data_out), .LD(and_5_out),
    .Dout({n16_bits_reg_1_dout_3, n16_bits_reg_1_dout_2, n16_bits_reg_1_dout}));
  not not_36 (not_36_out, cpu_1_addrbus[2]);
  not not_37 (not_37_out, cpu_1_addrbus[1]);
  Hex_Digit_Display hex_digit_display_3 (.value(n16_bits_reg_1_dout[3:0]));  // open: dp
  Hex_Digit_Display hex_digit_display_4 (.value(n16_bits_reg_1_dout[7:4]));  // open: dp

  // Notes on the sheet:
  //   Memory Chip (2K)
endmodule

module CPU (
  input  INT,
  input  [15:0] DATA_IN,
  output INTACK,
  output MEMLD,
  output [11:0] ADDRBUS,
  output [15:0] DATA_OUT
);

  wire AluZF, INTLD, IRLD, MUX, PCINC, PCLD, PCMUX, REGLD, SP_minus_minus, SP_plus_plus, ZF, ZFLD, ZFPOP;
  wire [1:0] ARMUX, DATAMUX;
  wire [2:0] Dst;
  wire [5:0] AluCode;
  wire [5:3] IR;
  wire [11:0] adder_1_out, adder_2_out, IntRegOut, multiplexer_2_out, pc_1_dout, R7_12, Src2_12;
  wire [15:0] AluResult, bit_extender_1_out, regbank_1_r0, regbank_1_r1, regbank_1_r2, regbank_1_r3,
       regbank_1_r4, regbank_1_r5, regbank_1_r6, Result, Src1_16, ZFMemOut;
  wire [15:12] R7_16, Src2_16;

  CU cu_1 (
    .Opcode(DATA_IN[15:12]), .ZF(ZF), .PCMUX(PCMUX), .SP_plus_plus(SP_plus_plus),
    .SP_minus_minus(SP_minus_minus), .PCLD(PCLD), .PCINC(PCINC), .REGLD(REGLD), .ZFLD(ZFLD), .MUX(MUX),
    .MEMLD(MEMLD), .INTLD(INTLD), .ZFPOP(ZFPOP), .INTACK(INTACK), .INT(INT), .DATAMUX(DATAMUX),
    .ARMUX(ARMUX), .IRLD(IRLD));
  Multiplexer #(.select(2), .width(12), .enable("false")) multiplexer_1 (
    .in0(pc_1_dout), .in1(Src2_12), .in2(R7_12), .in3(IntRegOut), .out(ADDRBUS), .sel(ARMUX));
  PC pc_1 (.Din(multiplexer_2_out), .PCINC(PCINC), .PCLD(PCLD), .Dout(pc_1_dout));
  Multiplexer #(.width(12), .enable("false")) multiplexer_2 (
    .in0(adder_1_out), .in1(DATA_IN[11:0]), .out(multiplexer_2_out), .sel(PCMUX));
  Adder #(.width(12)) adder_1 (.a(pc_1_dout), .b({AluCode, IR, Dst}), .out(adder_1_out));  // open: cin, cout
  RegBank regbank_1 (
    .Din(Result), .REGSEL(Dst), .REGLD(REGLD), .SP_minus_minus(SP_minus_minus), .SP_plus_plus(SP_plus_plus),
    .R0(regbank_1_r0), .R1(regbank_1_r1), .R2(regbank_1_r2), .R3(regbank_1_r3), .R4(regbank_1_r4),
    .R5(regbank_1_r5), .R6(regbank_1_r6), .R7({R7_16, R7_12}));
  Multiplexer #(.select(3), .width(16), .enable("false")) multiplexer_3 (
    .in0(regbank_1_r0), .in1(regbank_1_r1), .in2(regbank_1_r2), .in3(regbank_1_r3), .in4(regbank_1_r4),
    .in5(regbank_1_r5), .in6(regbank_1_r6), .in7({R7_16, R7_12}), .out(Src1_16), .sel(AluCode[2:0]));
  ALU alu_1 (.A(Src1_16), .B({Src2_16, Src2_12}), .AluOp(AluCode), .AluResult(AluResult), .ZF(AluZF));
  Multiplexer #(.select(2), .width(16), .enable("false")) multiplexer_4 (
    .in0(Src1_16), .in1(bit_extender_1_out), .in2(ZFMemOut), .out(DATA_OUT), .sel(DATAMUX));  // open: in3
  assign bit_extender_1_out = {{4{1'b0}}, pc_1_dout};  // Bit_Extender bit_extender_1
  _12_bits_Reg InterReg (.Din(adder_2_out), .LD(INTLD), .Dout(IntRegOut));
  Multiplexer #(.select(3), .width(16), .enable("false")) multiplexer_5 (
    .in0(regbank_1_r0), .in1(regbank_1_r1), .in2(regbank_1_r2), .in3(regbank_1_r3), .in4(regbank_1_r4),
    .in5(regbank_1_r5), .in6(regbank_1_r6), .in7({R7_16, R7_12}), .out({Src2_16, Src2_12}), .sel(IR));
  Adder #(.width(12)) adder_2 (.a(12'h7f0), .b({{9{1'b0}}, DATA_IN[2:0]}), .out(adder_2_out));  // open: cin, cout
  IR ir_1 (.Din(DATA_IN[11:0]), .LD(IRLD), .Dout({AluCode, IR, Dst}));
  Multiplexer #(.width(16), .enable("false")) multiplexer_6 (.in0(AluResult), .in1(DATA_IN), .out(Result), .sel(MUX));
  ZF_Unit zf_unit_1 (.D_0(DATA_IN[0]), .ZFPOP(ZFPOP), .ZFLD(ZFLD), .ZFIN(AluZF), .ZF(ZF), .ZF_MEMOUT(ZFMemOut));

  // Other names for the same wires on the sheet: IR (some bits) = {AluCode, Dst}; Src1[2:0] = AluCode[2:0];
  //   Opcode[3:0] = DATA_IN[15:12]; Src2[2:0] = IR; R7_16[11:0] = R7_12; Src2_16[11:0] = Src2_12

  // Notes on the sheet:
  //   Address Decision
  //   PC_OUT
  //   Data Decision
  //   Interrupt Decision
  //   Register Bank & ALU
  //   Instruction Decoding
  //   ALU/LD MUX
  //   ZF Unit
endmodule

module _1_bit_Reg (
  input  Din,
  input  LD,
  output Dout
);

  wire and_1_out, and_2_out, Clk_out;

  Clock Clk (.out(Clk_out));
  and and_1 (and_1_out, Din, LD);
  and and_2 (and_2_out, ~Din, LD);  // AND_Gate
  S_R_Flip_Flop s_r_ff_1 (.S(and_1_out), .clk(Clk_out), .R(and_2_out), .Q(Dout));  // open: Qn, preset, reset, en
endmodule

module _2_bits_Reg (
  input  [1:0] Din,
  input  LD,
  output [1:0] Dout
);

  _1_bit_Reg u_1_bit_reg_1 (.Din(Din[0]), .LD(LD), .Dout(Dout[0]));
  _1_bit_Reg u_1_bit_reg_2 (.Din(Din[1]), .LD(LD), .Dout(Dout[1]));
endmodule

module _4_bits_Reg (
  input  [3:0] Din,
  input  LD,
  output [3:0] Dout
);

  _2_bits_Reg u_2_bits_reg_1 (.Din(Din[1:0]), .LD(LD), .Dout(Dout[1:0]));
  _2_bits_Reg u_2_bits_reg_2 (.Din(Din[3:2]), .LD(LD), .Dout(Dout[3:2]));
endmodule

module _5_bits_Reg (
  input  [4:0] Din,
  input  LD,
  output [4:0] Dout
);

  _4_bits_Reg u_4_bits_reg_1 (.Din(Din[3:0]), .LD(LD), .Dout(Dout[3:0]));
  _1_bit_Reg u_1_bit_reg_1 (.Din(Din[4]), .LD(LD), .Dout(Dout[4]));
endmodule

module _8_bits_Reg (
  input  [7:0] Din,
  input  LD,
  output [7:0] Dout
);

  _4_bits_Reg u_4_bits_reg_1 (.Din(Din[3:0]), .LD(LD), .Dout(Dout[3:0]));
  _4_bits_Reg u_4_bits_reg_2 (.Din(Din[7:4]), .LD(LD), .Dout(Dout[7:4]));
endmodule

module _10_bits_Reg (
  input  [9:0] Din,
  input  LD,
  output [9:0] Dout
);

  _8_bits_Reg u_8_bits_reg_1 (.Din(Din[7:0]), .LD(LD), .Dout(Dout[7:0]));
  _2_bits_Reg u_2_bits_reg_1 (.Din(Din[9:8]), .LD(LD), .Dout(Dout[9:8]));
endmodule

module _12_bits_Reg (
  input  [11:0] Din,
  input  LD,
  output [11:0] Dout
);

  _8_bits_Reg u_8_bits_reg_1 (.Din(Din[7:0]), .LD(LD), .Dout(Dout[7:0]));
  _4_bits_Reg u_4_bits_reg_1 (.Din(Din[11:8]), .LD(LD), .Dout(Dout[11:8]));
endmodule

module _16_bits_Reg (
  input  [15:0] Din,
  input  LD,
  output [15:0] Dout
);

  _8_bits_Reg u_8_bits_reg_1 (.Din(Din[7:0]), .LD(LD), .Dout(Dout[7:0]));
  _8_bits_Reg u_8_bits_reg_2 (.Din(Din[15:8]), .LD(LD), .Dout(Dout[15:8]));
endmodule

module Reg6 (
  input  [15:0] Din,
  input  INC,
  input  LD,
  output [15:0] Dout
);

  wire or_1_out;
  wire [15:0] adder_1_out, multiplexer_1_out;

  Multiplexer #(.width(16), .enable("false")) multiplexer_1 (
    .in0(Din), .in1(adder_1_out), .out(multiplexer_1_out), .sel(INC));
  or or_1 (or_1_out, INC, LD);
  _16_bits_Reg u_16_bits_reg_1 (.Din(multiplexer_1_out), .LD(or_1_out), .Dout(Dout));
  Adder #(.width(16)) adder_1 (.a(16'h1), .b(Dout), .out(adder_1_out));  // open: cin, cout
endmodule

module Reg7 (
  input  [15:0] Din,
  input  DEC,
  input  INC,
  input  LD,
  output [15:0] Dout
);

  wire or_1_out;
  wire [15:0] adder_1_out, multiplexer_1_out, subtractor_1_out;

  Multiplexer #(.select(2), .width(16), .enable("false")) multiplexer_1 (
    .in0(Din), .in1(adder_1_out), .in2(subtractor_1_out), .out(multiplexer_1_out), .sel({DEC, INC}));  // open: in3
  or or_1 (or_1_out, DEC, INC, LD);
  Subtractor #(.width(16)) subtractor_1 (.a(Dout), .b(16'h1), .out(subtractor_1_out));  // open: bin, bout
  Adder #(.width(16)) adder_1 (.a(16'h1), .b(Dout), .out(adder_1_out));  // open: cin, cout
  _16_bits_Reg u_16_bits_reg_1 (.Din(multiplexer_1_out), .LD(or_1_out), .Dout(Dout));
endmodule

module RegBank (
  input  [15:0] Din,
  input  [2:0] REGSEL,
  input  REGLD,
  input  SP_minus_minus,
  input  SP_plus_plus,
  output [15:0] R0,
  output [15:0] R1,
  output [15:0] R2,
  output [15:0] R3,
  output [15:0] R4,
  output [15:0] R5,
  output [15:0] R6,
  output [15:0] R7
);

  wire and_1_out, and_2_out, and_3_out, and_4_out, and_5_out, and_6_out, and_7_out, and_8_out,
       decoder_1_out0, decoder_1_out1, decoder_1_out2, decoder_1_out3, decoder_1_out4, decoder_1_out5,
       decoder_1_out6, decoder_1_out7;

  Decoder #(.select(3), .enable("false")) decoder_1 (
    .out0(decoder_1_out0), .out1(decoder_1_out1), .out2(decoder_1_out2), .out3(decoder_1_out3),
    .out4(decoder_1_out4), .out5(decoder_1_out5), .out6(decoder_1_out6), .out7(decoder_1_out7), .sel(REGSEL));
  and and_1 (and_1_out, decoder_1_out0, REGLD);
  and and_2 (and_2_out, decoder_1_out1, REGLD);
  and and_3 (and_3_out, decoder_1_out2, REGLD);
  and and_4 (and_4_out, decoder_1_out3, REGLD);
  and and_5 (and_5_out, decoder_1_out4, REGLD);
  and and_6 (and_6_out, decoder_1_out5, REGLD);
  and and_7 (and_7_out, decoder_1_out6, REGLD);
  and and_8 (and_8_out, decoder_1_out7, REGLD);
  _16_bits_Reg u_16_bits_reg_1 (.Din(Din), .LD(and_1_out), .Dout(R0));
  _16_bits_Reg u_16_bits_reg_2 (.Din(Din), .LD(and_2_out), .Dout(R1));
  _16_bits_Reg u_16_bits_reg_3 (.Din(Din), .LD(and_3_out), .Dout(R2));
  _16_bits_Reg u_16_bits_reg_4 (.Din(Din), .LD(and_4_out), .Dout(R3));
  _16_bits_Reg u_16_bits_reg_5 (.Din(Din), .LD(and_5_out), .Dout(R4));
  _16_bits_Reg u_16_bits_reg_6 (.Din(Din), .LD(and_6_out), .Dout(R5));
  _16_bits_Reg u_16_bits_reg_7 (.Din(Din), .LD(and_7_out), .Dout(R6));
  Reg7 reg7_1 (.Din(Din), .DEC(SP_minus_minus), .INC(SP_plus_plus), .LD(and_8_out), .Dout(R7));
endmodule

module ALU (
  input  [15:0] A,
  input  [15:0] B,
  input  [5:0] AluOp,
  output [15:0] AluResult,
  output ZF
);

  wire [15:0] adder_1_out, adder_2_out, and_1_out, multiplexer_1_out, not_1_out, or_1_out, subtractor_1_out,
       subtractor_2_out, xor_1_out;

  Adder #(.width(16)) adder_1 (.a(A), .b(B), .out(adder_1_out));  // open: cin, cout
  Subtractor #(.width(16)) subtractor_1 (.a(A), .b(B), .out(subtractor_1_out));  // open: bin, bout
  assign and_1_out = A & B;  // AND_Gate and_1, 16 bits wide
  assign or_1_out = A | B;  // OR_Gate or_1, 16 bits wide
  assign xor_1_out = A ^ B;  // XOR_Gate xor_1, 16 bits wide
  assign not_1_out = ~B;  // NOT_Gate not_1, 16 bits wide
  Adder #(.width(16)) adder_2 (.a(B), .b(16'h1), .out(adder_2_out));  // open: cin, cout
  Subtractor #(.width(16)) subtractor_2 (.a(B), .b(16'h1), .out(subtractor_2_out));  // open: bin, bout
  Multiplexer #(.select(3), .width(16), .enable("false")) multiplexer_1 (
    .in0(not_1_out), .in1(B), .in2(adder_2_out), .in3(subtractor_2_out), .out(multiplexer_1_out),
    .sel({1'b0, AluOp[1:0]}));  // open: in4, in5, in6, in7
  Multiplexer #(.select(3), .width(16), .enable("false")) multiplexer_2 (
    .in0(adder_1_out), .in1(subtractor_1_out), .in2(and_1_out), .in3(or_1_out), .in4(xor_1_out),
    .in7(multiplexer_1_out), .out(AluResult), .sel(AluOp[5:3]));  // open: in5, in6
  nor nor_1 (ZF, AluResult[0], AluResult[1], AluResult[2], AluResult[3], AluResult[4], AluResult[5], AluResult[6], AluResult[7], AluResult[9], AluResult[10], AluResult[11], AluResult[12], AluResult[13], AluResult[14], AluResult[15], AluResult[8]);

  // Notes on the sheet:
  //   Adder
  //   Substractor
  //   Bitwise AND
  //   Bitwise OR
  //   Bitwise XOR
  //   Bitwise NOT
  //   Move
  //   Increment
  //   Decrement
endmodule

module PC (
  input  [11:0] Din,
  input  PCINC,
  input  PCLD,
  output [11:0] Dout
);

  wire or_1_out;
  wire [11:0] adder_1_out, multiplexer_1_out;

  Adder #(.width(12)) adder_1 (.a(Dout), .b(12'h1), .out(adder_1_out));  // open: cin, cout
  Multiplexer #(.width(12), .enable("false")) multiplexer_1 (
    .in0(Din), .in1(adder_1_out), .out(multiplexer_1_out), .sel(PCINC));
  or or_1 (or_1_out, PCINC, PCLD);
  _12_bits_Reg u_12_bits_reg_1 (.Din(multiplexer_1_out), .LD(or_1_out), .Dout(Dout));
endmodule

module IR (
  input  [11:0] Din,
  input  LD,
  output [11:0] Dout
);

  _8_bits_Reg u_8_bits_reg_1 (.Din(Din[7:0]), .LD(LD), .Dout(Dout[7:0]));
  _4_bits_Reg u_4_bits_reg_1 (.Din(Din[11:8]), .LD(LD), .Dout(Dout[11:8]));
endmodule

module CU (
  input  [3:0] Opcode,
  input  INT,
  input  ZF,
  output ZFPOP,
  output INTLD,
  output MEMLD,
  output ZFLD,
  output PCLD,
  output PCINC,
  output REGLD,
  output MUX,
  output IRLD,
  output INTACK,
  output SP_minus_minus,
  output SP_plus_plus,
  output PCMUX,
  output [1:0] ARMUX,
  output [1:0] DATAMUX
);

  wire and_2_out, and_3_out, clock_1_out, INT_ACCEPT_q;
  wire [1:1] and_1_out;
  wire [3:0] multiplexer_1_out;
  wire [4:0] multiplexer_2_out, multiplexer_3_out, n5_bits_reg_1_dout;
  wire [24:0] Dout;

  and and_1 (and_1_out[1], ~Opcode[0], ~Opcode[1], Opcode[2], ~Opcode[3]);  // AND_Gate
  Multiplexer #(.select(2), .width(4), .enable("false")) multiplexer_1 (
    .in0(Opcode), .in1(Opcode), .in2(4'b0000), .in3(4'b0101), .out(multiplexer_1_out),
    .sel({and_1_out[1], ZF}));
  Multiplexer #(.width(5), .enable("false")) multiplexer_2 (
    .in0(Dout[4:0]), .in1({1'b0, multiplexer_1_out}), .out(multiplexer_2_out), .sel(Dout[24]));
  Multiplexer #(.width(5), .enable("false")) multiplexer_3 (
    .in0(multiplexer_2_out), .in1(5'b10011), .out(multiplexer_3_out), .sel(and_2_out));
  and and_2 (and_2_out, INT, INT_ACCEPT_q, and_3_out);
  and and_3 (and_3_out, ~Dout[4], ~Dout[3], ~Dout[2], ~Dout[1], ~Dout[0]);  // AND_Gate
  _5_bits_Reg u_5_bits_reg_1 (.Din(multiplexer_3_out), .LD(1'b1), .Dout(n5_bits_reg_1_dout));
  Clock clock_1 (.out(clock_1_out));
  ROM #(.addrWidth(5), .dataWidth(25)) rom_1 (
    .addr(n5_bits_reg_1_dout),
    .data({Dout[24], ZFPOP, INTLD, ARMUX, MEMLD, ZFLD, PCLD, PCINC, REGLD, MUX, IRLD, INTACK, SP_minus_minus, SP_plus_plus, PCMUX, DATAMUX, Dout[6:0]}));  // open: sel
  S_R_Flip_Flop INT_ACCEPT (
    .S(Dout[5]), .clk(clock_1_out), .R(Dout[6]), .Q(INT_ACCEPT_q));  // open: Qn, preset, reset, en

  // Other names for the same wires on the sheet: Dout[23:7] = {ZFPOP, INTLD, ARMUX, MEMLD, ZFLD, PCLD, PCINC, REGLD, MUX, IRLD, INTACK, SP_minus_minus, SP_plus_plus, PCMUX, DATAMUX};
  //   IFSET = Dout[5]; IFRST = Dout[6]; FETCH = Dout[24]; Next[4:0] = Dout[4:0]

  // Notes on the sheet:
  //   Fetch
  //   ISR (address of INT1)
  //   contents of rom_1 (hex, n*v repeats v):
  //   101201f 1c000 10c000 180000 0 20000 0 48000 280800 411 2a0880 412 20 40 40f a00410 220200 20c000
  //   220200 2808d4 681915 320200
endmodule

module ZF_Unit (
  input  [15:0] ZF_MEMOUT,
  input  D_0,
  input  ZFPOP,
  input  ZFLD,
  input  ZFIN,
  output ZF
);

  wire and_1_out, and_2_out, and_3_out, and_4_out, Clk_out, or_1_out, or_2_out;

  and and_1 (and_1_out, D_0, ZFPOP);
  and and_2 (and_2_out, ZFPOP, ~D_0);  // AND_Gate
  and and_3 (and_3_out, ZFLD, ZFIN);
  and and_4 (and_4_out, ~ZFIN, ZFLD);  // AND_Gate
  or or_1 (or_1_out, and_1_out, and_3_out);
  Clock Clk (.out(Clk_out));
  or or_2 (or_2_out, and_2_out, and_4_out);
  S_R_Flip_Flop s_r_ff_1 (.S(or_1_out), .clk(Clk_out), .R(or_2_out), .Q(ZF_MEMOUT[0]));  // open: Qn, preset, reset, en

  assign ZF = ZF_MEMOUT[0];
  // also tied to GND on the sheet: {ZF_MEMOUT[1], ZF_MEMOUT[2], ZF_MEMOUT[3], ZF_MEMOUT[4], ZF_MEMOUT[5], ZF_MEMOUT[6], ZF_MEMOUT[7], ZF_MEMOUT[8], ZF_MEMOUT[9], ZF_MEMOUT[10], ZF_MEMOUT[11], ZF_MEMOUT[12], ZF_MEMOUT[13], ZF_MEMOUT[14], ZF_MEMOUT[15]}
endmodule

module InputDeviceInt (
  input  [15:0] Data,
  input  Button,
  input  Select,
  output [15:0] DataOut,
  output INT
);

  wire and_1_out, and_2_out, clock_1_out;

  and and_1 (and_1_out, ~INT, Button);  // AND_Gate
  Clock clock_1 (.out(clock_1_out));
  and and_2 (and_2_out, Select, INT);
  S_R_Flip_Flop s_r_ff_1 (.S(and_1_out), .clk(clock_1_out), .R(and_2_out), .Q(INT));  // open: Qn, preset, reset, en

  assign DataOut = Data;
endmodule

module InputDevicePol (
  input  [15:0] Data,
  input  Button,
  input  Ready,
  input  A0,
  output [15:0] DataOut
);

  wire and_1_out, and_2_out, and_3_out, clock_1_out;
  wire [0:0] s_r_ff_1_q;

  and and_1 (and_1_out, ~s_r_ff_1_q[0], Button);  // AND_Gate
  and and_2 (and_2_out, and_3_out, s_r_ff_1_q[0]);
  and and_3 (and_3_out, Ready, ~A0);  // AND_Gate
  Multiplexer #(.width(16), .enable("false")) multiplexer_1 (
    .in0(Data), .in1({{15{1'b0}}, s_r_ff_1_q[0]}), .out(DataOut), .sel(A0));
  Clock clock_1 (.out(clock_1_out));
  S_R_Flip_Flop s_r_ff_1 (
    .S(and_1_out), .clk(clock_1_out), .R(and_2_out), .Q(s_r_ff_1_q[0]));  // open: Qn, preset, reset, en
endmodule

module PIC (
  input  DEVICE_0,
  input  DEVICE_1,
  input  DEVICE_2,
  input  DEVICE_3,
  input  DEVICE_4,
  input  DEVICE_5,
  input  DEVICE_6,
  input  DEVICE_7,
  output [15:0] DEVICE_ID,
  output INTERRUPT
);

  wire [2:0] priority_encoder_1_out;

  Priority_Encoder #(.disabled(0)) priority_encoder_1 (
    .in0(DEVICE_0), .in1(DEVICE_1), .in2(DEVICE_2), .in3(DEVICE_3), .in4(DEVICE_4), .in5(DEVICE_5),
    .in6(DEVICE_6), .in7(DEVICE_7), .out(priority_encoder_1_out), .gs(INTERRUPT));  // open: en_in, en_out
  assign DEVICE_ID = {{13{1'b0}}, priority_encoder_1_out};  // Bit_Extender bit_extender_1
endmodule
