// Logisim project hw1.circ as structural Verilog
module main (
  input  ld,
  input  clr
);

  wire [2:0] rom_1_data;
  wire [9:0] n10bit_pc_1_out;
  wire [12:3] rom_1_data_2;
  wire [15:0] alu_1_output, multiplexer_1_out, multiplexer_2_out, n8_16bit_register_bank_1_r0,
       n8_16bit_register_bank_1_r1, n8_16bit_register_bank_1_r2, n8_16bit_register_bank_1_r3,
       n8_16bit_register_bank_1_r4, n8_16bit_register_bank_1_r5, n8_16bit_register_bank_1_r6,
       n8_16bit_register_bank_1_r7;

  _10bit_PC u_10bit_pc_1 (.inc(1'b1), .load(ld), .clr(clr), .out(n10bit_pc_1_out));  // open: data
  _8_16bit_Register_Bank u_8_16bit_register_bank_1 (
    .data(alu_1_output), .reg_sel(rom_1_data), .load(1'b1), .R0(n8_16bit_register_bank_1_r0),
    .R1(n8_16bit_register_bank_1_r1), .R2(n8_16bit_register_bank_1_r2), .R3(n8_16bit_register_bank_1_r3),
    .R4(n8_16bit_register_bank_1_r4), .R5(n8_16bit_register_bank_1_r5), .R6(n8_16bit_register_bank_1_r6),
    .R7(n8_16bit_register_bank_1_r7));  // open: inc6, dec7, inc7
  ROM #(.addrWidth(10), .dataWidth(13)) rom_1 (.addr(n10bit_pc_1_out), .data({rom_1_data_2, rom_1_data}));  // open: sel
  Multiplexer #(.select(3), .width(16), .enable("false")) multiplexer_1 (
    .in0(n8_16bit_register_bank_1_r0), .in1(n8_16bit_register_bank_1_r1), .in2(n8_16bit_register_bank_1_r2),
    .in3(n8_16bit_register_bank_1_r3), .in4(n8_16bit_register_bank_1_r4), .in5(n8_16bit_register_bank_1_r5),
    .in6(n8_16bit_register_bank_1_r6), .in7(n8_16bit_register_bank_1_r7), .out(multiplexer_1_out),
    .sel(rom_1_data_2[12:10]));
  Multiplexer #(.select(3), .width(16), .enable("false")) multiplexer_2 (
    .in0(n8_16bit_register_bank_1_r0), .in1(n8_16bit_register_bank_1_r1), .in2(n8_16bit_register_bank_1_r2),
    .in3(n8_16bit_register_bank_1_r3), .in4(n8_16bit_register_bank_1_r4), .in5(n8_16bit_register_bank_1_r5),
    .in6(n8_16bit_register_bank_1_r6), .in7(n8_16bit_register_bank_1_r7), .out(multiplexer_2_out),
    .sel(rom_1_data_2[9:7]));
  ALU alu_1 (
    .Din1(multiplexer_1_out), .Din2(multiplexer_2_out), .\output (alu_1_output), .ALUop(rom_1_data_2[6:3]));  // open: ZF__zero_flag

  // Notes on the sheet:
  //   Data Memory
endmodule

module _1bit_SR_Reg (
  input  data,
  input  load,
  output \output 
);

  wire and_1_out, and_2_out, clk_out;

  Clock clk (.out(clk_out));
  and and_1 (and_1_out, data, load);
  and and_2 (and_2_out, ~data, load);  // AND_Gate
  S_R_Flip_Flop s_r_ff_1 (.S(and_1_out), .clk(clk_out), .R(and_2_out), .Q(\output ));  // open: Qn, preset, reset, en
endmodule

module _4bit_SR_Reg (
  input  [3:0] data,
  input  load,
  output [3:0] \output 
);

  _1bit_SR_Reg u_1bit_sr_reg_1 (.data(data[0]), .load(load), .\output (\output [0]));
  _1bit_SR_Reg u_1bit_sr_reg_2 (.data(data[1]), .load(load), .\output (\output [1]));
  _1bit_SR_Reg u_1bit_sr_reg_3 (.data(data[2]), .load(load), .\output (\output [2]));
  _1bit_SR_Reg u_1bit_sr_reg_4 (.data(data[3]), .load(load), .\output (\output [3]));
endmodule

module _8bit_SR_Reg (
  input  [7:0] data,
  input  load,
  output [7:0] \output 
);

  _4bit_SR_Reg u_4bit_sr_reg_1 (.data(data[3:0]), .load(load), .\output (\output [3:0]));
  _4bit_SR_Reg u_4bit_sr_reg_2 (.data(data[7:4]), .load(load), .\output (\output [7:4]));
endmodule

module _16bit_SR_Reg (
  input  [15:0] data,
  input  load,
  output [15:0] \output 
);

  _8bit_SR_Reg u_8bit_sr_reg_1 (.data(data[7:0]), .load(load), .\output (\output [7:0]));
  _8bit_SR_Reg u_8bit_sr_reg_2 (.data(data[15:8]), .load(load), .\output (\output [15:8]));
endmodule

module _8_16bit_Register_Bank (
  input  [15:0] data,
  input  [2:0] reg_sel,
  input  load,
  input  inc6,
  input  dec7,
  input  inc7,
  output [15:0] R0,
  output [15:0] R1,
  output [15:0] R2,
  output [15:0] R3,
  output [15:0] R4,
  output [15:0] R5,
  output [15:0] R6,
  output [15:0] R7
);

  wire and_1_out, and_2_out, and_3_out, and_4_out, and_5_out, and_6_out, and_7_out, and_8_out,
       decoder_1_out0, decoder_1_out1, decoder_1_out2, decoder_1_out3, decoder_1_out4, decoder_1_out5,
       decoder_1_out6, decoder_1_out7;

  Decoder #(.select(3)) decoder_1 (
    .out0(decoder_1_out0), .out1(decoder_1_out1), .out2(decoder_1_out2), .out3(decoder_1_out3),
    .out4(decoder_1_out4), .out5(decoder_1_out5), .out6(decoder_1_out6), .out7(decoder_1_out7), .sel(reg_sel));  // open: en
  and and_1 (and_1_out, decoder_1_out0, load);
  and and_2 (and_2_out, decoder_1_out1, load);
  and and_3 (and_3_out, decoder_1_out2, load);
  and and_4 (and_4_out, decoder_1_out3, load);
  and and_5 (and_5_out, decoder_1_out4, load);
  and and_6 (and_6_out, decoder_1_out5, load);
  and and_7 (and_7_out, decoder_1_out6, load);
  and and_8 (and_8_out, decoder_1_out7, load);
  _16bit_SR_Reg u_16bit_sr_reg_1 (.data(data), .load(and_1_out), .\output (R0));
  _16bit_SR_Reg u_16bit_sr_reg_2 (.data(data), .load(and_2_out), .\output (R1));
  _16bit_SR_Reg u_16bit_sr_reg_3 (.data(data), .load(and_3_out), .\output (R2));
  _16bit_SR_Reg u_16bit_sr_reg_4 (.data(data), .load(and_4_out), .\output (R3));
  _16bit_SR_Reg u_16bit_sr_reg_5 (.data(data), .load(and_5_out), .\output (R4));
  _16bit_SR_Reg u_16bit_sr_reg_6 (.data(data), .load(and_6_out), .\output (R5));
  _16bit_reg_w_inc u_16bit_reg_w_inc_1 (.data(data), .increment(inc6), .load(and_7_out), .\output (R6));
  _16bit_reg_w_inc___dec u_16bit_reg_w_inc_dec_1 (.data(data), .dec(dec7), .inc(inc7), .load(and_8_out), .\output (R7));

  // Notes on the sheet:
  //   0
  //   1
  //   2
  //   3
  //   4
  //   5
endmodule

module _1bit_reg_w_inc (
  input  data,
  input  increment,
  input  load,
  output \output 
);

  wire adder_1_out, multiplexer_1_out, or_1_out;

  Multiplexer multiplexer_1 (.in0(data), .in1(adder_1_out), .out(multiplexer_1_out), .sel(increment));  // open: en
  or or_1 (or_1_out, increment, load);
  Adder #(.width(1)) adder_1 (.a(1'b1), .b(\output ), .out(adder_1_out));  // open: cin, cout
  _1bit_SR_Reg u_1bit_sr_reg_1 (.data(multiplexer_1_out), .load(or_1_out), .\output (\output ));
endmodule

module _1bit_reg_w_inc___dec (
  input  data,
  input  dec,
  input  inc,
  input  load,
  output \output 
);

  wire adder_1_out, multiplexer_1_out, or_1_out, subtractor_1_out;

  Multiplexer #(.select(2)) multiplexer_1 (
    .in0(data), .in1(adder_1_out), .in2(subtractor_1_out), .in3(1'b0), .out(multiplexer_1_out),
    .sel({dec, inc}));  // open: en
  _1bit_SR_Reg u_1bit_sr_reg_1 (.data(multiplexer_1_out), .load(or_1_out), .\output (\output ));
  or or_1 (or_1_out, dec, inc, load);
  Subtractor #(.width(1)) subtractor_1 (.a(1'b1), .b(\output ), .out(subtractor_1_out));  // open: bin, bout
  Adder #(.width(1)) adder_1 (.a(1'b1), .b(\output ), .out(adder_1_out));  // open: cin, cout
endmodule

module _16bit_reg_w_inc (
  input  [15:0] data,
  input  increment,
  input  load,
  output [15:0] \output 
);

  wire or_1_out;
  wire [15:0] adder_1_out, multiplexer_1_out;

  Multiplexer #(.width(16)) multiplexer_1 (
    .in0(data), .in1(adder_1_out), .out(multiplexer_1_out), .sel(increment));  // open: en
  or or_1 (or_1_out, increment, load);
  _16bit_SR_Reg u_16bit_sr_reg_1 (.data(multiplexer_1_out), .load(or_1_out), .\output (\output ));
  Adder #(.width(16)) adder_1 (.a(16'h1), .b(\output ), .out(adder_1_out));  // open: cin, cout
endmodule

module _16bit_reg_w_inc___dec (
  input  [15:0] data,
  input  dec,
  input  inc,
  input  load,
  output [15:0] \output 
);

  wire or_1_out;
  wire [15:0] adder_1_out, multiplexer_1_out, subtractor_1_out;

  Multiplexer #(.select(2), .width(16)) multiplexer_1 (
    .in0(data), .in1(adder_1_out), .in2(subtractor_1_out), .out(multiplexer_1_out), .sel({dec, inc}));  // open: in3, en
  or or_1 (or_1_out, dec, inc, load);
  Subtractor #(.width(16)) subtractor_1 (.a(\output ), .b(16'h1), .out(subtractor_1_out));  // open: bin, bout
  Adder #(.width(16)) adder_1 (.a(16'h1), .b(\output ), .out(adder_1_out));  // open: cin, cout
  _16bit_SR_Reg u_16bit_sr_reg_1 (.data(multiplexer_1_out), .load(or_1_out), .\output (\output ));
endmodule

module ALU (
  input  [15:0] Din1,
  input  [15:0] Din2,
  input  [3:0] ALUop,
  output ZF__zero_flag,
  output [15:0] \output 
);

  wire [15:0] adder_1_out, adder_2_out, and_1_out, not_1_out, or_1_out, subtractor_1_out, subtractor_2_out,
       xor_1_out;

  Adder #(.width(16)) adder_1 (.a(Din1), .b(Din2), .out(adder_1_out));  // open: cin, cout
  Subtractor #(.width(16)) subtractor_1 (.a(Din1), .b(Din2), .out(subtractor_1_out));  // open: bin, bout
  assign and_1_out = Din1 & Din2;  // AND_Gate and_1, 16 bits wide
  assign or_1_out = Din1 | Din2;  // OR_Gate or_1, 16 bits wide
  assign xor_1_out = Din1 ^ Din2;  // XOR_Gate xor_1, 16 bits wide
  assign not_1_out = ~Din1;  // NOT_Gate not_1, 16 bits wide
  Adder #(.width(16)) adder_2 (.a(Din1), .b(16'h1), .out(adder_2_out));  // open: cin, cout
  Subtractor #(.width(16)) subtractor_2 (.a(Din1), .b(16'h1), .out(subtractor_2_out));  // open: bin, bout
  Multiplexer #(.select(4), .width(16)) multiplexer_1 (
    .in0(adder_1_out), .in1(subtractor_1_out), .in2(and_1_out), .in3(or_1_out), .in4(xor_1_out),
    .in5(not_1_out), .in6(Din1), .in7(adder_2_out), .in8(subtractor_2_out), .out(\output ), .sel(ALUop));  // open: in9, in10, in11, in12, in13, in14, in15, en
  nor nor_1 (ZF__zero_flag, \output [0], \output [1], \output [2], \output [3], \output [4], \output [5], \output [6], \output [7], \output [8], \output [9], \output [10], \output [11], \output [12], \output [13], \output [14], \output [15]);
endmodule

module _10bit_PC (
  input  [9:0] data,
  input  inc,
  input  load,
  input  clr,
  output [9:0] out
);

  wire clk_out;
  wire [9:0] adder_1_out, multiplexer_1_out;

  Adder #(.width(10)) adder_1 (.a(out), .b(10'h1), .out(adder_1_out));  // open: cin, cout
  Clock clk (.out(clk_out));
  Register #(.width(10)) Register (.D(multiplexer_1_out), .en(load), .Q(out), .clk(clk_out), .clr(clr));
  Multiplexer #(.width(10), .enable("false")) multiplexer_1 (
    .in0(data), .in1(adder_1_out), .out(multiplexer_1_out), .sel(inc));
endmodule
